// Logisim project processor.circ as structural Verilog: 8 circuits, main circuit main
module main (
  output [9:0] out_1
);

  wire and_2_out, Clear, Clear_Memory_out, Clock, clock_1_out, Enable, Finish, or_1_out;
  wire [2:0] instruction_divider_1_rd, instruction_divider_1_rs, instruction_divider_1_rt, multiplexer_1_out;
  wire [3:0] instruction_memory_1_out_6, registers_1_selected_register_output,
       registers_1_selected_register_output_2, registers_1_selected_register_output_3,
       registers_1_selected_register_output_4;
  wire [4:0] instruction_divider_1_opcode;
  wire [23:0] alu_1_output, instruction_divider_1_immediate, memory_1_dataread, multiplexer_2_out,
       multiplexer_3_out, multiplexer_4_out, registers_1_rd_rs_data_output, registers_1_rt_data_output;
  wire [23:4] instruction_memory_1_out_6_2;
  wire [23:16] registers_1_selected_register_output_5;
  wire [31:0] instruction_memory_1_instruction;

  Clock clock_1 (.out(clock_1_out));
  Button button_1 (.out(Clear));
  Hex_Digit_Display hex_digit_display_1 (.value(registers_1_selected_register_output_5[23:20]));  // open: dp
  and and_1 (Clock, clock_1_out, Enable);
  Hex_Digit_Display hex_digit_display_2 (.value(registers_1_selected_register_output_4));  // open: dp
  Hex_Digit_Display hex_digit_display_3 (.value(registers_1_selected_register_output_5[19:16]));  // open: dp
  Hex_Digit_Display hex_digit_display_4 (.value(instruction_memory_1_out_6_2[7:4]));  // open: dp
  Hex_Digit_Display hex_digit_display_5 (.value(instruction_memory_1_out_6));  // open: dp
  or or_1 (or_1_out, and_2_out, out_1[8]);
  Hex_Digit_Display hex_digit_display_6 (.value(registers_1_selected_register_output_3));  // open: dp
  Hex_Digit_Display hex_digit_display_7 (.value(registers_1_selected_register_output_2));  // open: dp
  Instruction_Memory instruction_memory_1 (
    .Clear(Clear), .Instruction(instruction_memory_1_instruction), .Jump(or_1_out),
    .Address(instruction_divider_1_immediate),
    .out_6({instruction_memory_1_out_6_2, instruction_memory_1_out_6}), .Clock(Clock), .Finish(Finish));
  and and_2 (and_2_out, out_1[7], alu_1_output[0]);
  Hex_Digit_Display hex_digit_display_8 (.value(registers_1_selected_register_output));  // open: dp
  Instruction_Divider instruction_divider_1 (
    .Instruction(instruction_memory_1_instruction), .Immediate(instruction_divider_1_immediate),
    .Rs(instruction_divider_1_rs), .Rd(instruction_divider_1_rd), .Opcode(instruction_divider_1_opcode),
    .Rt(instruction_divider_1_rt));
  Control control_1 (
    .a(instruction_divider_1_opcode[4]), .b(instruction_divider_1_opcode[3]), .WriteReg(out_1[9]),
    .c(instruction_divider_1_opcode[2]), .d(instruction_divider_1_opcode[1]),
    .e(instruction_divider_1_opcode[0]), .Jump(out_1[8]), .Branch(out_1[7]), .ALUSrc(out_1[6]),
    .ALUOp2(out_1[5]), .ALUOp1(out_1[4]), .ALUOp0(out_1[3]), .MemStore(out_1[2]), .MemReg(out_1[1]),
    .Finish(Finish), .MemSrc(out_1[0]));
  Multiplexer #(.width(3)) multiplexer_1 (
    .in0(instruction_divider_1_rt), .in1(instruction_divider_1_immediate[2:0]), .out(multiplexer_1_out),
    .sel(out_1[0]), .en(1'b1));
  Registers registers_1 (
    .in_1(Clock), .RD_Register(instruction_divider_1_rd), .in_3(Clear), .in_5(out_1[9]),
    .Data_Input(multiplexer_4_out), .Rd_Rs_Data_output(registers_1_rd_rs_data_output),
    .RS_Register(instruction_divider_1_rs), .Rt_Data_output(registers_1_rt_data_output),
    .RT_Register(multiplexer_1_out), .DataSrc(out_1[6]),
    .Selected_Register_output({registers_1_selected_register_output_5, registers_1_selected_register_output_4, registers_1_selected_register_output_3, registers_1_selected_register_output_2, registers_1_selected_register_output}));
  Multiplexer #(.width(24)) multiplexer_2 (
    .in0(registers_1_rt_data_output), .in1(instruction_divider_1_immediate), .out(multiplexer_2_out),
    .sel(out_1[6]), .en(1'b1));
  Multiplexer #(.width(24)) multiplexer_3 (
    .in0(instruction_divider_1_immediate), .in1(registers_1_rt_data_output), .out(multiplexer_3_out),
    .sel(out_1[0]), .en(1'b1));
  ALU alu_1 (
    .A(registers_1_rd_rs_data_output), .B(multiplexer_2_out), .ALUOp(out_1[5:3]), .Output(alu_1_output),
    .Branch(out_1[7]));
  Memory memory_1 (
    .DataStored(registers_1_rd_rs_data_output), .Load_Store(out_1[2]), .Address(multiplexer_3_out),
    .Enable(1'b1), .Clock(Clock), .Clear(Clear_Memory_out), .DataRead(memory_1_dataread));
  Button Clear_Memory (.out(Clear_Memory_out));
  Multiplexer #(.width(24)) multiplexer_4 (
    .in0(alu_1_output), .in1(memory_1_dataread), .out(multiplexer_4_out), .sel(out_1[1]), .en(1'b1));

  // Other names for the same wires on the sheet: MemSrc = out_1[0]; MemReg = out_1[1]; MemStore = out_1[2];
  //   ALUOp[2:0] = out_1[5:3]; ALUSrc = out_1[6]; Branch = out_1[7]; Jump = out_1[8]; RegWrite = out_1[9]
endmodule

module Instruction_Memory (
  input  Jump,
  input  [23:0] Address,
  input  Clock,
  input  Clear,
  input  Finish,
  output [23:0] out_6,
  output [31:0] Instruction
);

  wire and_1_out, not_1_out;
  wire [23:0] adder_1_out, multiplexer_1_out;

  not not_1 (not_1_out, Finish);
  and and_1 (and_1_out, Clock, not_1_out);
  Multiplexer #(.width(24)) multiplexer_1 (
    .in0(adder_1_out), .in1(Address), .out(multiplexer_1_out), .sel(Jump), .en(1'b1));
  Register #(.width(24)) PC (.D(multiplexer_1_out), .en(1'b1), .Q(out_6), .clk(and_1_out), .clr(Clear));
  Adder #(.width(24)) adder_1 (.a(out_6), .b(24'h1), .out(adder_1_out));  // open: cin, cout
  ROM #(.addrWidth(24), .dataWidth(32)) rom_1 (.addr(out_6), .data(Instruction), .sel(1'b1));

  // Notes on the sheet:
  //   contents of rom_1 (hex, n*v repeats v):
  //   18000002 30000000 280000ff 18000004 30000001 280000ff 18000003 30000002 280000ff 18000007 30000003
  //   280000ff 18000005 30000004 280000ff 18000000 1f000004 a9000000 18000001 aa000000 16e00000 4600001d
  //   15440000 4500001a 290000ff 1280000 18000001 aa000000 38000014 19000000 f9000000
endmodule

module Registers (
  input  in_1,
  input  [2:0] RD_Register,
  input  in_3,
  input  DataSrc,
  input  in_5,
  input  [2:0] RS_Register,
  input  [2:0] RT_Register,
  input  [23:0] Data_Input,
  output [23:0] Rd_Rs_Data_output,
  output [23:0] Selected_Register_output,
  output [23:0] Rt_Data_output
);

  wire R1, R2, R3, R4, R5, R6, R7, R8;
  wire [2:0] multiplexer_2_out;
  wire [23:0] demultiplexer_2_out0, demultiplexer_2_out1, demultiplexer_2_out2, demultiplexer_2_out3,
       demultiplexer_2_out4, demultiplexer_2_out5, demultiplexer_2_out6, demultiplexer_2_out7, register_1_q,
       register_2_q, register_3_q, register_4_q, register_5_q, register_6_q, register_7_q, register_8_q;

  Demultiplexer #(.select(3)) demultiplexer_1 (
    .out0(R1), .out1(R2), .out2(R3), .out3(R4), .out4(R5), .out5(R6), .out6(R7), .out7(R8), .in(in_5),
    .sel(RD_Register), .en(1'b1));
  Demultiplexer #(.select(3), .width(24)) demultiplexer_2 (
    .out0(demultiplexer_2_out0), .out1(demultiplexer_2_out1), .out2(demultiplexer_2_out2),
    .out3(demultiplexer_2_out3), .out4(demultiplexer_2_out4), .out5(demultiplexer_2_out5),
    .out6(demultiplexer_2_out6), .out7(demultiplexer_2_out7), .in(Data_Input), .sel(RD_Register), .en(1'b1));
  Register #(.width(24)) register_1 (.D(demultiplexer_2_out0), .en(R1), .Q(register_1_q), .clk(in_1), .clr(in_3));
  Register #(.width(24)) register_2 (.D(demultiplexer_2_out1), .en(R2), .Q(register_2_q), .clk(in_1), .clr(in_3));
  Register #(.width(24)) register_3 (.D(demultiplexer_2_out2), .en(R3), .Q(register_3_q), .clk(in_1), .clr(in_3));
  Register #(.width(24)) register_4 (.D(demultiplexer_2_out3), .en(R4), .Q(register_4_q), .clk(in_1), .clr(in_3));
  Register #(.width(24)) register_5 (.D(demultiplexer_2_out4), .en(R5), .Q(register_5_q), .clk(in_1), .clr(in_3));
  Register #(.width(24)) register_6 (.D(demultiplexer_2_out5), .en(R6), .Q(register_6_q), .clk(in_1), .clr(in_3));
  Register #(.width(24)) register_7 (.D(demultiplexer_2_out6), .en(R7), .Q(register_7_q), .clk(in_1), .clr(in_3));
  Register #(.width(24)) register_8 (.D(demultiplexer_2_out7), .en(R8), .Q(register_8_q), .clk(in_1), .clr(in_3));
  Multiplexer #(.select(3), .width(24)) multiplexer_1 (
    .in0(register_1_q), .in1(register_2_q), .in2(register_3_q), .in3(register_4_q), .in4(register_5_q),
    .in5(register_6_q), .in6(register_7_q), .in7(register_8_q), .out(Rd_Rs_Data_output),
    .sel(multiplexer_2_out), .en(1'b1));
  Multiplexer #(.width(3)) multiplexer_2 (
    .in0(RS_Register), .in1(RD_Register), .out(multiplexer_2_out), .sel(DataSrc), .en(1'b1));
  Multiplexer #(.select(3), .width(24)) multiplexer_3 (
    .in0(register_1_q), .in1(register_2_q), .in2(register_3_q), .in3(register_4_q), .in4(register_5_q),
    .in5(register_6_q), .in6(register_7_q), .in7(register_8_q), .out(Rt_Data_output), .sel(RT_Register),
    .en(1'b1));

  assign Selected_Register_output = Rd_Rs_Data_output;

  // Other names for the same wires on the sheet: Clear = in_3; Clock = in_1; Rd[2:0] = RD_Register; RegWrite = in_5;
  //   Rs[2:0] = RS_Register; Rt[2:0] = RT_Register
endmodule

module Instruction_Divider (
  input  [31:0] Instruction,
  output [23:0] Immediate,
  output [2:0] Rt,
  output [2:0] Rs,
  output [2:0] Rd,
  output [4:0] Opcode
);


  assign Immediate = Instruction[23:0];
  assign Opcode = Instruction[31:27];
  assign Rd = Instruction[26:24];
  assign Rs = Instruction[23:21];
  assign Rt = Instruction[20:18];
endmodule

module ALU (
  input  [23:0] A,
  input  [2:0] ALUOp,
  input  [23:0] B,
  input  Branch,
  output [23:0] Output
);

  wire [0:0] EQ, LT, MT;
  wire [23:0] adder_1_out, divider_1_out, multiplexer_1_out, multiplier_1_out, subtractor_1_out;

  Multiplexer #(.width(24)) multiplexer_1 (.in0(B), .in1(24'h1), .out(multiplexer_1_out), .sel(Branch), .en(1'b1));
  Adder #(.width(24)) adder_1 (.a(A), .b(B), .out(adder_1_out));  // open: cin, cout
  Subtractor #(.width(24)) subtractor_1 (.a(A), .b(B), .out(subtractor_1_out));  // open: bin, bout
  Comparator #(.width(24)) comparator_1 (.a(A), .b(multiplexer_1_out), .gt(MT[0]), .eq(EQ[0]), .lt(LT[0]));
  Multiplier #(.width(24)) multiplier_1 (.a(A), .b(B), .out(multiplier_1_out));  // open: cin, cout
  Divider #(.width(24)) divider_1 (.a(A), .b(B), .out(divider_1_out));  // open: upper, rem
  Multiplexer #(.select(3), .width(24)) multiplexer_2 (
    .in0(adder_1_out), .in1(subtractor_1_out), .in2({{23{1'b0}}, EQ[0]}), .in3({{23{1'b0}}, LT[0]}),
    .in4(multiplier_1_out), .in5(divider_1_out), .in6({{23{1'b0}}, MT[0]}), .out(Output), .sel(ALUOp),
    .en(1'b1));  // open: in7

  // Other names for the same wires on the sheet: Bit_0 = ALUOp[0]; Bit_1 = ALUOp[1]; Bit_2 = ALUOp[2];
  //   tunnel_t = EQ[0]; tunnel = LT[0]; tunnel_t_t = MT[0]
endmodule

module Memory (
  input  [23:0] DataStored,
  input  Load_Store,
  input  [23:0] Address,
  input  Enable,
  input  Clock,
  input  Clear,
  output [23:0] DataRead
);

  wire not_1_out;

  assign DataRead = Load_Store ? DataStored : 24'bz;  // Controlled_Buffer controlled_buffer_1
  not not_1 (not_1_out, Load_Store);
  RAM #(.addrWidth(24), .dataWidth(24)) ram_1 (
    .addr(Address), .data(DataRead), .sel(Enable), .clk(Clock), .ld(not_1_out), .clr(Clear));
endmodule

module Control (
  input  a,
  input  b,
  input  c,
  input  d,
  input  e,
  output WriteReg,
  output Jump,
  output Branch,
  output ALUSrc,
  output ALUOp2,
  output ALUOp1,
  output ALUOp0,
  output MemStore,
  output MemReg,
  output Finish,
  output MemSrc
);

  wire and_2_out, and_3_out, and_4_out, and_5_out, and_8_out, and_9_out, and_10_out, and_11_out, and_12_out,
       and_13_out, and_14_out, and_15_out, and_16_out, and_17_out, and_18_out, and_21_out, and_22_out,
       and_23_out, and_24_out, not_1_out, not_2_out, not_3_out, not_4_out, not_5_out, not_6_out, not_7_out,
       not_8_out, not_9_out, not_10_out, not_11_out, not_12_out, not_13_out, not_14_out, not_15_out,
       not_16_out, not_17_out, not_18_out, not_19_out, not_20_out, not_21_out, not_22_out, not_23_out,
       not_24_out, not_25_out, not_26_out, not_27_out, not_28_out, not_29_out, not_30_out, not_31_out,
       not_32_out, not_33_out, not_34_out, not_35_out;

  not not_1 (not_1_out, b);
  not not_2 (not_2_out, c);
  not not_3 (not_3_out, c);
  not not_4 (not_4_out, c);
  not not_5 (not_5_out, d);
  not not_6 (not_6_out, b);
  not not_7 (not_7_out, c);
  not not_8 (not_8_out, d);
  not not_9 (not_9_out, e);
  not not_10 (not_10_out, d);
  not not_11 (not_11_out, e);
  not not_12 (not_12_out, c);
  not not_13 (not_13_out, c);
  not not_14 (not_14_out, d);
  not not_15 (not_15_out, b);
  not not_16 (not_16_out, b);
  not not_17 (not_17_out, e);
  not not_18 (not_18_out, c);
  not not_19 (not_19_out, d);
  not not_20 (not_20_out, e);
  not not_21 (not_21_out, b);
  not not_22 (not_22_out, d);
  not not_23 (not_23_out, a);
  not not_24 (not_24_out, e);
  not not_25 (not_25_out, d);
  not not_26 (not_26_out, e);
  not not_27 (not_27_out, b);
  and and_1 (Finish, a, c, d, e);
  not not_28 (not_28_out, a);
  not not_29 (not_29_out, d);
  not not_30 (not_30_out, a);
  not not_31 (not_31_out, e);
  not not_32 (not_32_out, b);
  not not_33 (not_33_out, d);
  not not_34 (not_34_out, b);
  not not_35 (not_35_out, e);
  and and_2 (and_2_out, not_1_out, not_2_out);
  and and_3 (and_3_out, not_3_out, e);
  and and_4 (and_4_out, not_4_out, d);
  and and_5 (and_5_out, c, not_5_out);
  and and_6 (Jump, not_6_out, c, d, e);
  and and_7 (Branch, b, not_7_out, not_8_out, not_9_out);
  and and_8 (and_8_out, d, e);
  and and_9 (and_9_out, b, not_10_out, not_11_out);
  and and_10 (and_10_out, b, not_12_out, e);
  and and_11 (and_11_out, b, not_13_out, d);
  and and_12 (and_12_out, b, c, not_14_out);
  and and_13 (and_13_out, a, not_15_out);
  and and_14 (and_14_out, not_16_out, d, not_17_out);
  and and_15 (and_15_out, b, not_18_out, not_19_out, not_20_out);
  and and_16 (and_16_out, not_21_out, not_22_out, e);
  and and_17 (and_17_out, not_23_out, d, not_24_out);
  and and_18 (and_18_out, c, not_25_out);
  and and_19 (MemStore, c, d, not_26_out);
  and and_20 (MemReg, not_27_out, c, e);
  and and_21 (and_21_out, not_28_out, b, c, not_29_out, e);
  and and_22 (and_22_out, not_30_out, b, c, d, not_31_out);
  and and_23 (and_23_out, a, not_32_out, c, not_33_out, e);
  and and_24 (and_24_out, a, not_34_out, c, d, not_35_out);
  or or_1 (WriteReg, and_2_out, and_3_out, and_4_out, and_5_out);
  or or_2 (ALUSrc, and_8_out, c, and_9_out);
  or or_3 (ALUOp2, and_10_out, and_11_out, and_12_out, and_13_out);
  or or_4 (ALUOp1, and_14_out, and_15_out);
  or or_5 (ALUOp0, and_16_out, and_17_out, and_18_out);
  or or_6 (MemSrc, and_21_out, and_22_out, and_23_out, and_24_out);
endmodule

module fds (
  output [2:0] ALUOp
);
endmodule
